// Logisim project d_latch.circ as structural Verilog: 1 circuit, main circuit main
module main (
  input  D,
  input  en,
  input  d_in,
  input  en_in,
  output Q,
  output Q_bar,
  output q_out,
  output q_bar_out
);

  wire nand_1_out, nand_2_out, not_1_out;

  not not_1 (not_1_out, D);
  // VhdlEntity #(.content("library ieee;\nuse ieee.std_logic_1164.all;\n\nentity d_latch is\n    port (\n        d     : in  std_logic;\n        en    : in  std_logic;\n        q     : out std_logic;\n        q_bar : out std_logic\n    );\nend entity d_latch;\n\narchitecture behavioral of d_latch is\n    signal q_int : std_logic := '0';\nbegin\n    process (d, en)\n    begin\n        if en = '1' then\n            q_int <= d;\n        end if;\n    end process;\n    q     <= q_int;\n    q_bar <= not q_int;\nend architecture behavioral;")) vhdlentity_1: pin names not known; wires that end beside it: d_in, en_in, q_out, q_bar_out
  nand nand_1 (nand_1_out, D, en);
  nand nand_2 (nand_2_out, en, not_1_out);
  nand nand_3 (Q, nand_1_out, Q_bar);
  nand nand_4 (Q_bar, nand_2_out, Q);
endmodule
