// Logisim project jk_ff.circ as structural Verilog: 1 circuit, main circuit main
module main (
  input  J,
  input  clk,
  input  K,
  input  j_in,
  input  k_in,
  input  clk_in,
  output Q,
  output Q_bar,
  output q_out,
  output q_bar_out
);

  // VhdlEntity #(.content("library ieee;\nuse ieee.std_logic_1164.all;\n\nentity jk_ff is\n    port (\n        j     : in  std_logic;\n        k     : in  std_logic;\n        clk   : in  std_logic;\n        q     : out std_logic;\n        q_bar : out std_logic\n    );\nend entity jk_ff;\n\narchitecture behavioral of jk_ff is\n    signal q_int : std_logic := '0';\nbegin\n    process (clk)\n    begin\n        if rising_edge(clk) then\n            if (j = '0' and k = '0') then\n                q_int <= q_int;\n            elsif (j = '0' and k = '1') then\n                q_int <= '0';\n            elsif (j = '1' and k = '0') then\n                q_int <= '1';\n            elsif (j = '1' and k = '1') then\n                q_int <= not q_int;\n            end if;\n        end if;\n    end process;\n    q     <= q_int;\n    q_bar <= not q_int;\nend architecture behavioral;")) vhdlentity_1: pin names not known; wires that end beside it: J, clk, K, j_in, k_in, clk_in, q_out, q_bar_out
  // NAND_Gate nand_1 is placed but not wired
  // NAND_Gate nand_2 is placed but not wired
  // NAND_Gate nand_3 is placed but not wired
  // NAND_Gate nand_4 is placed but not wired
  // NAND_Gate nand_5 is placed but not wired
  // NAND_Gate nand_6 is placed but not wired
  // NAND_Gate nand_7 is placed but not wired
  // NAND_Gate nand_8 is placed but not wired
endmodule
