// Logisim project rs_latch.circ as structural Verilog: 1 circuit, main circuit main
module main (
  input  R,
  input  S,
  input  r_in,
  input  s_in,
  output Q,
  output Q_bar,
  output q_out,
  output q_bar_out
);

  // VhdlEntity #(.content("library ieee;\nuse ieee.std_logic_1164.all;\n\nentity rs_latch is\n    port (\n        r      : in  std_logic;\n        s      : in  std_logic;\n        q      : out std_logic;\n        q_bar  : out std_logic\n    );\nend entity rs_latch;\n\narchitecture behavioral of rs_latch is\n    signal q_int     : std_logic := '0';\n    signal q_bar_int : std_logic := '1';\nbegin\n    q_int     <= r nor q_bar_int;\n    q_bar_int <= s nor q_int;\n    q     <= q_int;\n    q_bar <= q_bar_int;\nend architecture behavioral;")) vhdlentity_1: pin names not known; wires that end beside it: r_in, s_in, q_out, q_bar_out
  nor nor_1 (Q, R, Q_bar);
  nor nor_2 (Q_bar, Q, S);
endmodule
